# Fritzing sketch arduino-nano (saved by Fritzing 0.9.4)

parts:
  Nano1 = Arduino Nano v2.3
  S2 = Round Pushbutton
  LED2 = RGB LED (com. cathode, rgb) [package="5 mm [THT]"]

nets:
  N1: Nano1.GND, S2.leg0, LED2.common_cathode
  N2: Nano1.D9, LED2.blue_anode
  N3: Nano1.D10, LED2.green_anode
  N4: Nano1.D11, LED2.red_anode
  N5: Nano1.D12, S2.leg1
